# Fritzing sketch rfid-keypad (saved by Fritzing 0.9.3b)

parts:
  Part1 = RFID-RC522-v2
  Part2 = Arduino Uno (Rev3) - ICSP
  Matrix_keypad1 = KEYPAD 4x4

nets:
  N1: Part1.SDA, Part2.D10_PWM/SS
  N2: Part1.SCK, Part2.D13/SCK
  N3: Part1.MOSI, Part2.D11_PWM/MOSI
  N4: Part1.MISO, Part2.ICSP_MISO, Part2.D12/MISO
  GND: Part1.GND, Part2.GND
  N5: Part1.RST, Part2.D9_PWM
  3.3V: Part1.3.3V, Part2.3V3
  N6: Part2.A0, Matrix_keypad1.col1
  N7: Part2.D8, Matrix_keypad1.col2
  N8: Part2.D2, Matrix_keypad1.row4
  N9: Part2.D3_PWM, Matrix_keypad1.row3
  N10: Part2.D4, Matrix_keypad1.row2
  N11: Part2.D5_PWM, Matrix_keypad1.row1
  N12: Part2.D6_PWM, Matrix_keypad1.col4
  N13: Part2.D7, Matrix_keypad1.col3

custom parts:
  RFID-RC522-v2: A simple China made RFID-RC522 Reader; do check the pin labels, as this is a MFRC522 based clone.
  KEYPAD 4x4: Matrix keypad 16 buttons, 4 rows x 4 columns
